# Fritzing sketch finalprojectcircuit (saved by Fritzing 0.9.5d)
breadboards: 3

parts:
  Part1 = Arduino Uno (Rev3) - ICSP
  VCC1 = Battery  # not connected
  J1 = Piezo Speaker
  J2 = Piezo Speaker
  HC-SR04_Sensor_1 = HC-SR04 Ultrasonic Distance Sensor
  Part2 = Breakout Board for Electret Microphone
  R1 = PHOTOCELL [package=photocell-kit]
  LED1 = RGB LED - (4 legs) [package="5 mm [THT]"]
  S1 = Pushbutton [package="[THT]"]
  R2 = Resistor [tolerance=±5% resistance=220 package=THT]
  R4 = Resistor [tolerance=±5% resistance=220 package=THT]
  R5 = Resistor [tolerance=±5% resistance=220 package="0603 [SMD]"]
  R6 = Resistor [tolerance=±5% resistance=220 package="0603 [SMD]"]
  R7 = Resistor [tolerance=±5% resistance=220 package="0603 [SMD]"]
  R8 = Resistor [tolerance=±5% resistance=220 package="1206 [SMD]"]
  R10 = Resistor [tolerance=±5% resistance=220 package="0603 [SMD]"]
  R12 = Resistor [tolerance=±5% resistance=220 package="0603 [SMD]"]
  R13 = Resistor [tolerance=±5% resistance=220 package="0603 [SMD]"]
  R14 = Resistor [tolerance=±5% resistance=220 package="0603 [SMD]"]
  R15 = Resistor [tolerance=±5% resistance=220 package="0603 [SMD]"]
  R16 = Resistor [tolerance=±5% resistance=220 package="0603 [SMD]"]
  R17 = Resistor [tolerance=±5% resistance=220 package="0603 [SMD]"]
  R18 = Resistor [tolerance=±5% resistance=220 package="0603 [SMD]"]
  LED2 = LED - 5mm [color="Red (633nm)" package="5 mm [THT]"]
  LED4 = LED - 5mm [color="Red (633nm)" package="5 mm [THT]"]
  LED5 = LED - 5mm [color="Red (633nm)" package="5 mm [THT]"]
  LED6 = LED - 5mm [color="Red (633nm)" package="5 mm [THT]"]
  LED7 = LED - 5mm [color="Red (633nm)" package="5 mm [THT]"]
  LED8 = LED - 5mm [color="Red (633nm)" package="5 mm [THT]"]
  LED9 = LED - 5mm [color="Red (633nm)" package="5 mm [THT]"]
  LED10 = LED - 5mm [color="Red (633nm)" package="5 mm [THT]"]
  LED11 = LED - 5mm [color="Red (633nm)" package="5 mm [THT]"]
  LED12 = LED - 5mm [color="Red (633nm)" package="5 mm [THT]"]
  R19 = Resistor [tolerance=±5% resistance=220 package=THT]
  LED13 = LED - 5mm [color="Red (633nm)" package="5 mm [THT]"]
  R20 = Resistor [tolerance=±5% resistance=220 package=THT]
  LED14 = smd LED [color="Red (633nm)" package="0805 [SMD]"]

nets:
  N1: Part1.A0, R1.P$2, R2.Pin_0
  N2: Part1.A1, Part2.AUD
  N3: Part1.ICSP_MOSI, Part1.D11_PWM/MOSI, LED4.cathode, LED5.cathode, LED7.cathode, LED8.cathode, LED9.cathode, LED10.cathode, LED11.cathode, LED12.cathode, LED13.cathode
  N4: Part1.D8, HC-SR04_Sensor_1.TRIG
  N5: Part1.D9_PWM, HC-SR04_Sensor_1.ECHO
  N6: Part1.D12/MISO, J1.pin2
  N7: Part1.D13/SCK, LED14.cathode
  N8: Part1.D2, R5.Pin_1
  N9: Part1.D3_PWM, R7.Pin_1
  N10: Part1.D4, R6.Pin_1
  N11: Part1.D6_PWM, J2.pin2
  N12: Part1.D7, S1.Pin_1, S1.Pin_2, R4.Pin_0
  VCC: Part1.5V, HC-SR04_Sensor_1.VCC, Part2.VCC, R1.P$1, S1.Pin_3, S1.Pin_4
  GND: Part1.GND, J1.pin1, J2.pin1, HC-SR04_Sensor_1.GND, Part2.GND, R2.Pin_1, R4.Pin_1, R10.Pin_1, R12.Pin_1, R13.Pin_1, R14.Pin_1, R15.Pin_1, R16.Pin_1, R17.Pin_0, R18.Pin_1, R19.Pin_1, R20.Pin_1, LED14.anode
  N13: LED1.red_cathode, R5.Pin_0
  N14: LED1.green_cathode, R6.Pin_0
  N15: LED1.blue_cathode, R7.Pin_0
  N16: R8.Pin_0, LED13.anode
  N17: R10.Pin_0, LED4.anode
  N18: R12.Pin_0, LED6.anode
  N19: R13.Pin_0, LED7.anode
  N20: R14.Pin_0, LED12.anode
  N21: R15.Pin_0, LED11.anode
  N22: R16.Pin_0, LED10.anode
  N23: R17.Pin_1, LED9.anode
  N24: R18.Pin_0, LED8.anode
  N25: LED2.anode, R19.Pin_0
  N26: LED5.anode, R20.Pin_0

notes:
  yellow line - pin connection
  Red line - power connection
  black line - ground connection
  Since there is no laser transmitter
  I used a red LED to indicate laser.
  [Since there is no laser transmitter
  I used a red LED to indicate laser.
